# Fritzing sketch zamok (saved by Fritzing 0.9.2b)
breadboards: 1

parts:
  S2 = Momentary Switch [package=ksa_sealed_tac_switch]
  S3 = Momentary Switch [package=ksa_sealed_tac_switch]
  Part1 = Arduino Nano (Rev3.0)
  S1 = Momentary Switch [package=ksa_sealed_tac_switch]
  LED1 = LED - 5mm [color="Red (633nm)" package="5 mm [THT]"]
  LED2 = LED - 5mm [color="Red (633nm)" package="5 mm [THT]"]
  R1 = Resistor [tolerance=±5% resistance=220 package=THT]
  J1 = Basic Servo

nets:
  N1: S2.2, Part1.D11/MOSI
  N2: S2.4, S3.4, Part1.D2, S1.4
  N3: S3.2, Part1.D10
  N4: Part1.D8, R1.Pin_1
  N5: Part1.D12/MISO, S1.2
  N6: Part1.D13/SCK, J1.pulse
  N7: LED1.cathode, LED2.anode, R1.Pin_0
  N8: LED1.anode, LED2.cathode

// code stored in the sketch: zamok.ino
void setup() {

}

void loop() {

}
