# Fritzing sketch sketch (saved by Fritzing 0.9.3b)
breadboards: 1

parts:
  WeMos_D1_Mini1 = WeMos D1 Mini
  Squix1 = OLED 0.96" 128x64 I2C SSD1306
  U1 = SUP500F [package=sup500f]
  S1 = SWITCH-MOMENTARY-2 [package=tactile-pth]
  R1 = Resistor [tolerance=±5% resistance=220 package=THT]

nets:
  VCC: WeMos_D1_Mini1.5V, Squix1.VCC, U1.VCC, R1.Pin_1
  N1: WeMos_D1_Mini1.D0, S1.1, R1.Pin_0
  N2: WeMos_D1_Mini1.D1, Squix1.SCL
  N3: WeMos_D1_Mini1.D2, Squix1.SCA
  N4: WeMos_D1_Mini1.D6, U1.TX-O
  N5: WeMos_D1_Mini1.D7, U1.RX-I
  GND: WeMos_D1_Mini1.G, Squix1.GND, U1.GND, S1.2

custom parts:
  WeMos D1 Mini: The D1 mini is a mini wifi board based on ESP-8266EX.
