# Fritzing sketch speed limiter arv (saved by Fritzing 0.9.3b)
perfboards: 1

parts:
  Part1 = Arduino Nano (Rev3.0)
  Squix1 = OLED 0.96" 128x64 I2C SSD1306

nets:
  GND: Part1.GND, Squix1.GND
  5V: Part1.5V, Squix1.VCC
  N1: Part1.A5, Squix1.SCL
  N2: Part1.A4, Squix1.SCA
